// Digital circuit Registers_DRAM.dig as structural Verilog
module Registers_DRAM (
  input  PC_orind,
  input  [3:0] Address,
  input  [3:0] Input_MEM,
  input  [1:0] ctrl_MEM__Load__Store__Reset,
  input  [1:0] ctrl_PC__Load__INC__Reset,
  input  ctrl_IR__Load__Store__Reset,
  input  clk,
  output [3:0] Output
);

  wire [3:0] memory_1_output, multiplexer_1_out, pc_1_output;

  Multiplexer #(.Bits(4)) multiplexer_1 (.sel(PC_orind), .in_0(pc_1_output), .in_1(Address), .out(multiplexer_1_out));
  memory memory_1 (
    .clk(clk), .\input (Input_MEM), .CTRL(ctrl_MEM__Load__Store__Reset), .Address(multiplexer_1_out),
    .\output (memory_1_output));
  PC pc_1 (.clk(clk), .CTRL(ctrl_PC__Load__INC__Reset), .\output (pc_1_output));
  IR ir_1 (.clk(clk), .Input(memory_1_output), .CTRL(ctrl_IR__Load__Store__Reset), .\output (Output));
endmodule
