// Digital circuit memory.dig as structural Verilog
module memory (
  input  clk,
  input  [3:0] \input ,
  input  [1:0] CTRL,
  input  [3:0] Address,
  output [3:0] \output 
);

  wire and_1_out, and_2_out, and_3_out, and_4_out, and_5_out, and_6_out, and_7_out, and_8_out, and_9_out,
       and_10_out, and_11_out, and_12_out, and_13_out, and_14_out, and_15_out, and_16_out, decoder_1_out_0,
       decoder_1_out_1, decoder_1_out_2, decoder_1_out_3, decoder_1_out_4, decoder_1_out_5, decoder_1_out_6,
       decoder_1_out_7, decoder_1_out_8, decoder_1_out_9, decoder_1_out_10, decoder_1_out_11,
       decoder_1_out_12, decoder_1_out_13, decoder_1_out_14, decoder_1_out_15;
  wire [3:0] gpr_1_output, gpr_2_output, gpr_3_output, gpr_4_output, gpr_5_output, gpr_6_output,
       gpr_7_output, gpr_8_output, gpr_9_output, gpr_10_output, gpr_11_output, gpr_12_output, gpr_13_output,
       gpr_14_output, gpr_15_output, gpr_16_output;

  Decoder #(.Selector_Bits(4)) decoder_1 (
    .sel(Address), .out_0(decoder_1_out_0), .out_1(decoder_1_out_1), .out_2(decoder_1_out_2),
    .out_3(decoder_1_out_3), .out_4(decoder_1_out_4), .out_5(decoder_1_out_5), .out_6(decoder_1_out_6),
    .out_7(decoder_1_out_7), .out_8(decoder_1_out_8), .out_9(decoder_1_out_9), .out_10(decoder_1_out_10),
    .out_11(decoder_1_out_11), .out_12(decoder_1_out_12), .out_13(decoder_1_out_13),
    .out_14(decoder_1_out_14), .out_15(decoder_1_out_15));
  and and_1 (and_1_out, clk, decoder_1_out_0);
  and and_2 (and_2_out, clk, decoder_1_out_1);
  and and_3 (and_3_out, clk, decoder_1_out_2);
  and and_4 (and_4_out, clk, decoder_1_out_3);
  and and_5 (and_5_out, clk, decoder_1_out_4);
  and and_6 (and_6_out, clk, decoder_1_out_5);
  and and_7 (and_7_out, clk, decoder_1_out_6);
  and and_8 (and_8_out, clk, decoder_1_out_7);
  and and_9 (and_9_out, clk, decoder_1_out_8);
  and and_10 (and_10_out, clk, decoder_1_out_9);
  and and_11 (and_11_out, clk, decoder_1_out_10);
  and and_12 (and_12_out, clk, decoder_1_out_11);
  and and_13 (and_13_out, clk, decoder_1_out_12);
  and and_14 (and_14_out, clk, decoder_1_out_13);
  and and_15 (and_15_out, clk, decoder_1_out_14);
  and and_16 (and_16_out, clk, decoder_1_out_15);
  GPR gpr_1 (.clk(and_1_out), .INPUT(\input ), .CTRL(CTRL), .\output (gpr_1_output));
  GPR gpr_2 (.clk(and_2_out), .INPUT(\input ), .CTRL(CTRL), .\output (gpr_2_output));
  GPR gpr_3 (.clk(and_3_out), .INPUT(\input ), .CTRL(CTRL), .\output (gpr_3_output));
  GPR gpr_4 (.clk(and_4_out), .INPUT(\input ), .CTRL(CTRL), .\output (gpr_4_output));
  GPR gpr_5 (.clk(and_5_out), .INPUT(\input ), .CTRL(CTRL), .\output (gpr_5_output));
  GPR gpr_6 (.clk(and_6_out), .INPUT(\input ), .CTRL(CTRL), .\output (gpr_6_output));
  GPR gpr_7 (.clk(and_7_out), .INPUT(\input ), .CTRL(CTRL), .\output (gpr_7_output));
  GPR gpr_8 (.clk(and_8_out), .INPUT(\input ), .CTRL(CTRL), .\output (gpr_8_output));
  GPR gpr_9 (.clk(and_9_out), .INPUT(\input ), .CTRL(CTRL), .\output (gpr_9_output));
  GPR gpr_10 (.clk(and_10_out), .INPUT(\input ), .CTRL(CTRL), .\output (gpr_10_output));
  GPR gpr_11 (.clk(and_11_out), .INPUT(\input ), .CTRL(CTRL), .\output (gpr_11_output));
  GPR gpr_12 (.clk(and_12_out), .INPUT(\input ), .CTRL(CTRL), .\output (gpr_12_output));
  GPR gpr_13 (.clk(and_13_out), .INPUT(\input ), .CTRL(CTRL), .\output (gpr_13_output));
  GPR gpr_14 (.clk(and_14_out), .INPUT(\input ), .CTRL(CTRL), .\output (gpr_14_output));
  GPR gpr_15 (.clk(and_15_out), .INPUT(\input ), .CTRL(CTRL), .\output (gpr_15_output));
  GPR gpr_16 (.clk(and_16_out), .INPUT(\input ), .CTRL(CTRL), .\output (gpr_16_output));
  Multiplexer #(.Bits(4), .Selector_Bits(4)) multiplexer_1 (
    .sel(Address), .in_0(gpr_1_output), .in_1(gpr_2_output), .in_2(gpr_3_output), .in_3(gpr_4_output),
    .in_4(gpr_5_output), .in_5(gpr_6_output), .in_6(gpr_7_output), .in_7(gpr_8_output), .in_8(gpr_9_output),
    .in_9(gpr_10_output), .in_10(gpr_11_output), .in_11(gpr_12_output), .in_12(gpr_13_output),
    .in_13(gpr_14_output), .in_14(gpr_15_output), .in_15(gpr_16_output), .out(\output ));
endmodule
